// Logisim project connect4_circuit.circ as structural Verilog: 24 circuits, main circuit connect_four
module connect_four_display (
);

  wire button_1_out, button_2_out, button_3_out, button_4_out, button_5_out, button_6_out, button_7_out,
       Reset_out;
  wire [1:0] connect_four_1_p, connect_four_1_w;
  wire [6:0] connect_four_1_c0, connect_four_1_c1, connect_four_1_c2, connect_four_1_c3, connect_four_1_c4,
       connect_four_1_c5, connect_four_1_c6;

  Button Reset (.out(Reset_out));
  connect_four connect_four_1 (
    .R(Reset_out), .I0(button_1_out), .I1(button_2_out), .I2(button_3_out), .I3(button_4_out),
    .I4(button_5_out), .I5(button_6_out), .I6(button_7_out), .P(connect_four_1_p), .W(connect_four_1_w),
    .C0(connect_four_1_c0), .C1(connect_four_1_c1), .C2(connect_four_1_c2), .C3(connect_four_1_c3),
    .C4(connect_four_1_c4), .C5(connect_four_1_c5), .C6(connect_four_1_c6));
  Button button_1 (.out(button_1_out));
  Button button_2 (.out(button_2_out));
  Button button_3 (.out(button_3_out));
  Button button_4 (.out(button_4_out));
  column_rgb column_rgb_1 (.C(connect_four_1_c0));
  column_rgb column_rgb_2 (.C(connect_four_1_c1));
  column_rgb column_rgb_3 (.C(connect_four_1_c2));
  column_rgb column_rgb_4 (.C(connect_four_1_c3));
  Button button_5 (.out(button_5_out));
  Button button_6 (.out(button_6_out));
  Button button_7 (.out(button_7_out));
  player_display player_display_1 (.in_1(connect_four_1_w));
  player_display player_display_2 (.in_1(connect_four_1_p));
  column_rgb column_rgb_5 (.C(connect_four_1_c4));
  column_rgb column_rgb_6 (.C(connect_four_1_c5));
  column_rgb column_rgb_7 (.C(connect_four_1_c6));

  // Notes on the sheet:
  //   Play
endmodule

module connect_four (
  input  R,
  input  I0,
  input  I1,
  input  I2,
  input  I3,
  input  I4,
  input  I5,
  input  I6,
  output [1:0] P,
  output [1:0] W,
  output [6:0] C0,
  output [6:0] C1,
  output [6:0] C2,
  output [6:0] C3,
  output [6:0] C4,
  output [6:0] C5,
  output [6:0] C6
);

  wire and_1_out, buffer_1_out, buffer_2_out, buffer_3_out, buffer_4_out, buffer_5_out, buffer_6_out,
       buffer_7_out, buffer_8_out, buffer_9_out, move_1_valid, nor_1_out, not_1_out, one_tick_pulse_1_x,
       one_tick_pulse_2_x, one_tick_pulse_3_x, one_tick_pulse_4_x, one_tick_pulse_5_x, one_tick_pulse_6_x,
       one_tick_pulse_7_x, or_1_out, Winner_over;
  wire [1:0] not_2_out;
  wire [2:0] priority_encoder_1_out;
  wire [48:0] move_1_s_new, multiplexer_1_out, reset_state_1_out_1;

  one_tick_pulse one_tick_pulse_1 (.A(I0), .X(one_tick_pulse_1_x));
  one_tick_pulse one_tick_pulse_2 (.A(I1), .X(one_tick_pulse_2_x));
  one_tick_pulse one_tick_pulse_3 (.A(I2), .X(one_tick_pulse_3_x));
  one_tick_pulse one_tick_pulse_4 (.A(I3), .X(one_tick_pulse_4_x));
  one_tick_pulse one_tick_pulse_5 (.A(I4), .X(one_tick_pulse_5_x));
  one_tick_pulse one_tick_pulse_6 (.A(I5), .X(one_tick_pulse_6_x));
  one_tick_pulse one_tick_pulse_7 (.A(I6), .X(one_tick_pulse_7_x));
  game_over_check Winner (.S({C0, C1, C2, C3, C4, C5, C6}), .Over(Winner_over), .P(W));
  buf buffer_1 (buffer_1_out, one_tick_pulse_7_x);
  buf buffer_2 (buffer_2_out, one_tick_pulse_6_x);
  buf buffer_3 (buffer_3_out, one_tick_pulse_5_x);
  buf buffer_4 (buffer_4_out, one_tick_pulse_4_x);
  buf buffer_5 (buffer_5_out, one_tick_pulse_3_x);
  buf buffer_6 (buffer_6_out, one_tick_pulse_2_x);
  buf buffer_7 (buffer_7_out, one_tick_pulse_1_x);
  nor nor_1 (nor_1_out, one_tick_pulse_7_x, one_tick_pulse_6_x, one_tick_pulse_5_x, one_tick_pulse_4_x, one_tick_pulse_3_x, one_tick_pulse_2_x, one_tick_pulse_1_x);
  turn Player (.W(and_1_out), .R(R), .win(Winner_over), .P(P));
  Priority_Encoder priority_encoder_1 (
    .in0(buffer_1_out), .in1(buffer_2_out), .in2(buffer_3_out), .in3(buffer_4_out), .in4(buffer_5_out),
    .in5(buffer_6_out), .in6(buffer_7_out), .in7(nor_1_out), .out(priority_encoder_1_out), .en_in(1'b1));  // open: gs, en_out
  not not_1 (not_1_out, Winner_over);
  move move_1 (
    .P(P[1]), .S({C0, C1, C2, C3, C4, C5, C6}), .C(priority_encoder_1_out), .S_new(move_1_s_new),
    .Valid(move_1_valid));
  reset_state reset_state_1 (.out_1(reset_state_1_out_1));
  and and_1 (and_1_out, move_1_valid, not_1_out);
  color_decoder color_decoder_1 (.P(not_2_out));  // open: G, R, B
  not not_2 (not_2_out[0], W[1]);
  not not_3 (not_2_out[1], W[0]);
  Multiplexer #(.width(49)) multiplexer_1 (
    .in0(move_1_s_new), .in1(reset_state_1_out_1), .out(multiplexer_1_out), .sel(R));
  buf buffer_8 (buffer_8_out, R);
  or or_1 (or_1_out, buffer_8_out, and_1_out);
  state_memory state_memory_1 (.in_1(multiplexer_1_out), .W(buffer_9_out), .out_3({C0, C1, C2, C3, C4, C5, C6}));
  buf buffer_9 (buffer_9_out, or_1_out);
  // RGBLED rgbled_1: pin names not known
endmodule

module color_decoder (
  input  [1:0] P,
  output G,
  output R,
  output B
);

  not not_1 (G, P[1]);
  nand nand_1 (R, P[1], P[0]);
  nor nor_1 (B, P[1], P[0]);

  // Notes on the sheet:
  //   00 - empty
  //   10 - player 1
  //   01 - player 2
  //   11 - black
endmodule

module one_tick_pulse (
  input  A,
  output X
);

  wire not_1_out;

  and and_1 (X, A, not_1_out);
  not not_1 (not_1_out, A);
endmodule

module column_decoder (
  input  [6:0] C,
  output [1:0] R5,
  output [1:0] R4,
  output [1:0] R3,
  output [1:0] R2,
  output [1:0] R1,
  output [1:0] R0
);

  wire highest_bit_1_gt0, highest_bit_1_gt1, highest_bit_1_gt2, highest_bit_1_gt3, highest_bit_1_gt4,
       highest_bit_1_gt5, not_1_out, not_2_out, not_3_out, not_4_out, not_5_out, not_6_out;

  highest_bit highest_bit_1 (
    .C(C), .GT5(highest_bit_1_gt5), .GT4(highest_bit_1_gt4), .GT3(highest_bit_1_gt3),
    .GT2(highest_bit_1_gt2), .GT1(highest_bit_1_gt1), .GT0(highest_bit_1_gt0));  // open: EQ5, EQ4, EQ3, EQ2, EQ1, EQ0
  not not_1 (not_1_out, C[5]);
  not not_2 (not_2_out, C[4]);
  not not_3 (not_3_out, C[3]);
  not not_4 (not_4_out, C[2]);
  not not_5 (not_5_out, C[1]);
  not not_6 (not_6_out, C[0]);
  and and_1 (R5[0], not_1_out, highest_bit_1_gt5);
  and and_2 (R5[1], C[5], highest_bit_1_gt5);
  and and_3 (R4[0], not_2_out, highest_bit_1_gt4);
  and and_4 (R4[1], C[4], highest_bit_1_gt4);
  and and_5 (R3[0], not_3_out, highest_bit_1_gt3);
  and and_6 (R3[1], C[3], highest_bit_1_gt3);
  and and_7 (R2[0], not_4_out, highest_bit_1_gt2);
  and and_8 (R2[1], C[2], highest_bit_1_gt2);
  and and_9 (R1[0], not_5_out, highest_bit_1_gt1);
  and and_10 (R1[1], C[1], highest_bit_1_gt1);
  and and_11 (R0[0], not_6_out, highest_bit_1_gt0);
  and and_12 (R0[1], C[0], highest_bit_1_gt0);
endmodule

module column_rgb (
  input  [6:0] C
);

  wire [1:0] column_decoder_1_r0, column_decoder_1_r1, column_decoder_1_r2, column_decoder_1_r3,
       column_decoder_1_r4, column_decoder_1_r5;

  column_decoder column_decoder_1 (
    .C(C), .R5(column_decoder_1_r5), .R4(column_decoder_1_r4), .R3(column_decoder_1_r3),
    .R2(column_decoder_1_r2), .R1(column_decoder_1_r1), .R0(column_decoder_1_r0));
  color_decoder color_decoder_1 (.P(column_decoder_1_r5));  // open: G, R, B
  color_decoder color_decoder_2 (.P(column_decoder_1_r4));  // open: G, R, B
  color_decoder color_decoder_3 (.P(column_decoder_1_r3));  // open: G, R, B
  color_decoder color_decoder_4 (.P(column_decoder_1_r2));  // open: G, R, B
  color_decoder color_decoder_5 (.P(column_decoder_1_r1));  // open: G, R, B
  color_decoder color_decoder_6 (.P(column_decoder_1_r0));  // open: G, R, B
  // RGBLED rgbled_1: pin names not known
  // RGBLED rgbled_2: pin names not known
  // RGBLED rgbled_3: pin names not known
  // RGBLED rgbled_4: pin names not known
  // RGBLED rgbled_5: pin names not known
  // RGBLED rgbled_6: pin names not known
endmodule

module move_helper (
  input  P,
  input  [6:0] C,
  input  E,
  output Valid,
  output [6:0] C_new
);

  wire and_1_out, and_2_out, and_3_out, and_4_out, and_5_out, and_6_out, and_7_out, and_8_out, and_9_out,
       and_10_out, and_11_out, and_12_out, and_13_out, and_14_out, and_15_out, and_16_out, and_17_out,
       and_18_out, and_19_out, and_20_out, and_21_out, and_22_out, and_23_out, and_24_out, and_25_out,
       and_26_out, buffer_1_out, highest_bit_1_eq0, highest_bit_1_eq1, highest_bit_1_eq2, highest_bit_1_eq3,
       highest_bit_1_eq4, highest_bit_1_eq5, highest_bit_1_gt0, highest_bit_1_gt1, highest_bit_1_gt2,
       highest_bit_1_gt3, highest_bit_1_gt4, highest_bit_1_gt5, not_1_out, or_1_out, or_2_out, or_3_out,
       or_4_out, or_5_out, or_6_out, or_7_out;

  highest_bit highest_bit_1 (
    .C(C), .GT5(highest_bit_1_gt5), .EQ5(highest_bit_1_eq5), .GT4(highest_bit_1_gt4),
    .EQ4(highest_bit_1_eq4), .GT3(highest_bit_1_gt3), .EQ3(highest_bit_1_eq3), .GT2(highest_bit_1_gt2),
    .EQ2(highest_bit_1_eq2), .GT1(highest_bit_1_gt1), .EQ1(highest_bit_1_eq1), .GT0(highest_bit_1_gt0),
    .EQ0(highest_bit_1_eq0));
  and and_1 (and_1_out, C[5], highest_bit_1_gt5);
  and and_2 (and_2_out, C[4], highest_bit_1_gt4);
  and and_3 (and_3_out, C[3], highest_bit_1_gt3);
  and and_4 (and_4_out, C[2], highest_bit_1_gt2);
  and and_5 (and_5_out, C[1], highest_bit_1_gt1);
  and and_6 (and_6_out, C[0], highest_bit_1_gt0);
  and and_7 (and_7_out, P, highest_bit_1_eq5);
  and and_8 (and_8_out, P, highest_bit_1_eq4);
  and and_9 (and_9_out, P, highest_bit_1_eq3);
  and and_10 (and_10_out, P, highest_bit_1_eq2);
  and and_11 (and_11_out, P, highest_bit_1_eq1);
  and and_12 (and_12_out, P, highest_bit_1_eq0);
  buf buffer_1 (buffer_1_out, E);
  not not_1 (not_1_out, E);
  or or_1 (or_1_out, C[6], highest_bit_1_eq5);
  or or_2 (or_2_out, and_7_out, highest_bit_1_eq4, and_1_out);
  or or_3 (or_3_out, and_8_out, highest_bit_1_eq3, and_2_out);
  or or_4 (or_4_out, and_9_out, highest_bit_1_eq2, and_3_out);
  or or_5 (or_5_out, and_10_out, highest_bit_1_eq1, and_4_out);
  or or_6 (or_6_out, and_11_out, highest_bit_1_eq0, and_5_out);
  or or_7 (or_7_out, and_12_out, and_6_out);
  nand nand_1 (Valid, C[6], buffer_1_out);
  and and_13 (and_13_out, or_1_out, buffer_1_out);
  and and_14 (and_14_out, C[6], not_1_out);
  and and_15 (and_15_out, or_2_out, buffer_1_out);
  and and_16 (and_16_out, C[5], not_1_out);
  and and_17 (and_17_out, or_3_out, buffer_1_out);
  and and_18 (and_18_out, C[4], not_1_out);
  and and_19 (and_19_out, or_4_out, buffer_1_out);
  and and_20 (and_20_out, C[3], not_1_out);
  and and_21 (and_21_out, or_5_out, buffer_1_out);
  and and_22 (and_22_out, C[2], not_1_out);
  and and_23 (and_23_out, or_6_out, buffer_1_out);
  and and_24 (and_24_out, C[1], not_1_out);
  and and_25 (and_25_out, or_7_out, buffer_1_out);
  and and_26 (and_26_out, C[0], not_1_out);
  or or_8 (C_new[6], and_13_out, and_14_out);
  or or_9 (C_new[5], and_15_out, and_16_out);
  or or_10 (C_new[4], and_17_out, and_18_out);
  or or_11 (C_new[3], and_19_out, and_20_out);
  or or_12 (C_new[2], and_21_out, and_22_out);
  or or_13 (C_new[1], and_23_out, and_24_out);
  or or_14 (C_new[0], and_25_out, and_26_out);
endmodule

module move (
  input  P,
  input  [48:0] S,
  input  [2:0] C,
  output [48:0] S_new,
  output Valid
);

  wire buffer_1_out, buffer_2_out, buffer_3_out, decoder_1_out0, decoder_1_out1, decoder_1_out2,
       decoder_1_out3, decoder_1_out4, decoder_1_out5, decoder_1_out6, decoder_1_out7, not_1_out;
  wire [6:0] move_helper_1_valid;

  Decoder #(.select(3)) decoder_1 (
    .out0(decoder_1_out0), .out1(decoder_1_out1), .out2(decoder_1_out2), .out3(decoder_1_out3),
    .out4(decoder_1_out4), .out5(decoder_1_out5), .out6(decoder_1_out6), .out7(decoder_1_out7), .sel(C),
    .en(1'b1));
  not not_1 (not_1_out, decoder_1_out7);
  buf buffer_1 (buffer_1_out, not_1_out);
  buf buffer_2 (buffer_2_out, buffer_1_out);
  buf buffer_3 (buffer_3_out, buffer_2_out);
  move_helper move_helper_1 (
    .P(P), .C(S[48:42]), .E(decoder_1_out6), .Valid(move_helper_1_valid[0]), .C_new(S_new[48:42]));
  move_helper move_helper_2 (
    .P(P), .C(S[41:35]), .E(decoder_1_out5), .Valid(move_helper_1_valid[1]), .C_new(S_new[41:35]));
  move_helper move_helper_3 (
    .P(P), .C(S[34:28]), .E(decoder_1_out4), .Valid(move_helper_1_valid[2]), .C_new(S_new[34:28]));
  move_helper move_helper_4 (
    .P(P), .C(S[27:21]), .E(decoder_1_out3), .Valid(move_helper_1_valid[3]), .C_new(S_new[27:21]));
  move_helper move_helper_5 (
    .P(P), .C(S[20:14]), .E(decoder_1_out2), .Valid(move_helper_1_valid[4]), .C_new(S_new[20:14]));
  move_helper move_helper_6 (
    .P(P), .C(S[13:7]), .E(decoder_1_out1), .Valid(move_helper_1_valid[5]), .C_new(S_new[13:7]));
  move_helper move_helper_7 (.P(P), .C(S[6:0]), .E(decoder_1_out0), .Valid(move_helper_1_valid[6]), .C_new(S_new[6:0]));
  and and_1 (Valid, move_helper_1_valid[0], move_helper_1_valid[1], move_helper_1_valid[2], move_helper_1_valid[3], move_helper_1_valid[4], move_helper_1_valid[5], move_helper_1_valid[6], buffer_3_out);
endmodule

module state_memory (
  input  [48:0] in_1,
  input  W,
  output [48:0] out_3
);

  Register #(.width(49)) register_1 (.D(in_1), .en(1'b1), .clk(W), .Q(out_3), .clr(1'b0));
endmodule

module reset_state (
  output [48:0] out_1
);


  assign out_1 = 49'h40810204081;
endmodule

module turn (
  input  W,
  input  R,
  input  win,
  output [1:0] P
);

  wire d_ff_1_q, d_ff_1_qn, not_1_out;

  D_Flip_Flop d_ff_1 (.D(d_ff_1_qn), .clk(W), .Q(d_ff_1_q), .Qn(d_ff_1_qn), .preset(R), .reset(1'b0));
  not not_1 (not_1_out, win);
  and and_1 (P[0], not_1_out, d_ff_1_qn);
  and and_2 (P[1], not_1_out, d_ff_1_q);
endmodule

module invert_column (
  input  [6:0] in_1,
  output [6:0] out_2
);

  wire and_1_out, and_2_out, and_3_out, and_4_out, and_5_out, and_6_out, highest_bit_1_eq0,
       highest_bit_1_eq1, highest_bit_1_eq2, highest_bit_1_eq3, highest_bit_1_eq4, highest_bit_1_eq5,
       highest_bit_1_gt0, highest_bit_1_gt1, highest_bit_1_gt2, highest_bit_1_gt3, highest_bit_1_gt4,
       highest_bit_1_gt5, not_1_out, not_2_out, not_3_out, not_4_out, not_5_out, not_6_out;

  not not_1 (not_1_out, in_1[0]);
  not not_2 (not_2_out, in_1[1]);
  not not_3 (not_3_out, in_1[2]);
  highest_bit highest_bit_1 (
    .C(in_1), .GT5(highest_bit_1_gt5), .EQ5(highest_bit_1_eq5), .GT4(highest_bit_1_gt4),
    .EQ4(highest_bit_1_eq4), .GT3(highest_bit_1_gt3), .EQ3(highest_bit_1_eq3), .GT2(highest_bit_1_gt2),
    .EQ2(highest_bit_1_eq2), .GT1(highest_bit_1_gt1), .EQ1(highest_bit_1_eq1), .GT0(highest_bit_1_gt0),
    .EQ0(highest_bit_1_eq0));
  not not_4 (not_4_out, in_1[3]);
  not not_5 (not_5_out, in_1[4]);
  not not_6 (not_6_out, in_1[5]);
  and and_1 (and_1_out, not_6_out, highest_bit_1_gt5);
  and and_2 (and_2_out, not_5_out, highest_bit_1_gt4);
  and and_3 (and_3_out, not_4_out, highest_bit_1_gt3);
  and and_4 (and_4_out, not_3_out, highest_bit_1_gt2);
  and and_5 (and_5_out, not_2_out, highest_bit_1_gt1);
  and and_6 (and_6_out, not_1_out, highest_bit_1_gt0);
  or or_1 (out_2[5], and_1_out, highest_bit_1_eq5);
  or or_2 (out_2[4], and_2_out, highest_bit_1_eq4);
  or or_3 (out_2[3], and_3_out, highest_bit_1_eq3);
  or or_4 (out_2[2], and_4_out, highest_bit_1_eq2);
  or or_5 (out_2[1], and_5_out, highest_bit_1_eq1);
  or or_6 (out_2[0], and_6_out, highest_bit_1_eq0);

  assign out_2[6] = in_1[6];
endmodule

module invert_board (
  input  [48:0] S,
  output [48:0] S_inv
);

  invert_column invert_column_1 (.in_1(S[48:42]), .out_2(S_inv[48:42]));
  invert_column invert_column_2 (.in_1(S[41:35]), .out_2(S_inv[41:35]));
  invert_column invert_column_3 (.in_1(S[34:28]), .out_2(S_inv[34:28]));
  invert_column invert_column_4 (.in_1(S[27:21]), .out_2(S_inv[27:21]));
  invert_column invert_column_5 (.in_1(S[20:14]), .out_2(S_inv[20:14]));
  invert_column invert_column_6 (.in_1(S[13:7]), .out_2(S_inv[13:7]));
  invert_column invert_column_7 (.in_1(S[6:0]), .out_2(S_inv[6:0]));
endmodule

module highest_bit (
  input  [6:0] C,
  output GT5,
  output EQ5,
  output GT4,
  output EQ4,
  output GT3,
  output EQ3,
  output GT2,
  output EQ2,
  output GT1,
  output EQ1,
  output GT0,
  output EQ0
);

  wire [2:0] priority_encoder_1_out;

  Priority_Encoder priority_encoder_1 (
    .in0(C[0]), .in1(C[1]), .in2(C[2]), .in3(C[3]), .in4(C[4]), .in5(C[5]), .in6(C[6]), .in7(1'b0),
    .out(priority_encoder_1_out), .en_in(1'b1));  // open: gs, en_out
  Comparator #(.mode("unsigned"), .width(3)) comparator_1 (
    .a(priority_encoder_1_out), .b(3'b101), .gt(GT5), .eq(EQ5));  // open: lt
  Comparator #(.mode("unsigned"), .width(3)) comparator_2 (
    .a(priority_encoder_1_out), .b(3'b100), .gt(GT4), .eq(EQ4));  // open: lt
  Comparator #(.mode("unsigned"), .width(3)) comparator_3 (
    .a(priority_encoder_1_out), .b(3'b011), .gt(GT3), .eq(EQ3));  // open: lt
  Comparator #(.mode("unsigned"), .width(3)) comparator_4 (
    .a(priority_encoder_1_out), .b(3'b010), .gt(GT2), .eq(EQ2));  // open: lt
  Comparator #(.mode("unsigned"), .width(3)) comparator_5 (
    .a(priority_encoder_1_out), .b(3'b001), .gt(GT1), .eq(EQ1));  // open: lt
  Comparator #(.mode("unsigned"), .width(3)) comparator_6 (
    .a(priority_encoder_1_out), .b(3'b000), .gt(GT0), .eq(EQ0));  // open: lt
endmodule

module remove_highest_bit_column (
  input  [6:0] C,
  output [6:0] C_new
);

  wire highest_bit_1_gt0, highest_bit_1_gt1, highest_bit_1_gt2, highest_bit_1_gt3, highest_bit_1_gt4,
       highest_bit_1_gt5;

  highest_bit highest_bit_1 (
    .C(C), .GT5(highest_bit_1_gt5), .GT4(highest_bit_1_gt4), .GT3(highest_bit_1_gt3),
    .GT2(highest_bit_1_gt2), .GT1(highest_bit_1_gt1), .GT0(highest_bit_1_gt0));  // open: EQ5, EQ4, EQ3, EQ2, EQ1, EQ0
  and and_1 (C_new[5], highest_bit_1_gt5, C[5]);
  and and_2 (C_new[4], highest_bit_1_gt4, C[4]);
  and and_3 (C_new[3], highest_bit_1_gt3, C[3]);
  and and_4 (C_new[2], highest_bit_1_gt2, C[2]);
  and and_5 (C_new[1], highest_bit_1_gt1, C[1]);
  and and_6 (C_new[0], highest_bit_1_gt0, C[0]);

  assign C_new[6] = 1'b0;
endmodule

module remove_highest_bit_board (
  input  [48:0] S,
  output [48:0] S_new
);

  remove_highest_bit_column remove_highest_bit_column_1 (.C(S[48:42]), .C_new(S_new[48:42]));
  remove_highest_bit_column remove_highest_bit_column_2 (.C(S[41:35]), .C_new(S_new[41:35]));
  remove_highest_bit_column remove_highest_bit_column_3 (.C(S[34:28]), .C_new(S_new[34:28]));
  remove_highest_bit_column remove_highest_bit_column_4 (.C(S[27:21]), .C_new(S_new[27:21]));
  remove_highest_bit_column remove_highest_bit_column_5 (.C(S[20:14]), .C_new(S_new[20:14]));
  remove_highest_bit_column remove_highest_bit_column_6 (.C(S[13:7]), .C_new(S_new[13:7]));
  remove_highest_bit_column remove_highest_bit_column_7 (.C(S[6:0]), .C_new(S_new[6:0]));
endmodule

module game_over_check (
  input  [48:0] S,
  output Over,
  output [1:0] P
);

  wire draw_check_1_d, win_check_1_w, win_check_2_w;
  wire [48:0] invert_board_1_s_inv;

  invert_board invert_board_1 (.S(S), .S_inv(invert_board_1_s_inv));
  win_check win_check_1 (.S(S), .W(win_check_1_w));
  win_check win_check_2 (.S(invert_board_1_s_inv), .W(win_check_2_w));
  draw_check draw_check_1 (.S(S), .D(draw_check_1_d));
  or or_1 (Over, win_check_1_w, draw_check_1_d, win_check_2_w);
  or or_2 (P[1], draw_check_1_d, win_check_1_w);
  or or_3 (P[0], win_check_2_w, draw_check_1_d);
endmodule

module win_vertical (
  input  [48:0] S,
  output W
);

  wire [48:0] and_1_out;

  assign and_1_out = S & {S[47:0], 1'b0} & {S[46:0], 2'b00} & {S[45:0], 3'b000};  // AND_Gate and_1, 49 bits wide
  or or_1 (W, and_1_out[0], and_1_out[1], and_1_out[2], and_1_out[3], and_1_out[4], and_1_out[5], and_1_out[6], and_1_out[7], and_1_out[8], and_1_out[9], and_1_out[10], and_1_out[11], and_1_out[12], and_1_out[13], and_1_out[14], and_1_out[15], and_1_out[16], and_1_out[17], and_1_out[18], and_1_out[19], and_1_out[20], and_1_out[21], and_1_out[22], and_1_out[23], and_1_out[24], and_1_out[25], and_1_out[26], and_1_out[27], and_1_out[28], and_1_out[29], and_1_out[30], and_1_out[31], and_1_out[32], and_1_out[33], and_1_out[34], and_1_out[35], and_1_out[36], and_1_out[37], and_1_out[38], and_1_out[39], and_1_out[40], and_1_out[41], and_1_out[42], and_1_out[43], and_1_out[44], and_1_out[45], and_1_out[46], and_1_out[47], and_1_out[48]);
endmodule

module win_horizontal (
  input  [48:0] S,
  output W
);

  wire [48:0] and_1_out;

  assign and_1_out = S & {S[41:0], {7{1'b0}}} & {S[34:0], {14{1'b0}}} & {S[27:0], {21{1'b0}}};  // AND_Gate and_1, 49 bits wide
  or or_1 (W, and_1_out[0], and_1_out[1], and_1_out[2], and_1_out[3], and_1_out[4], and_1_out[5], and_1_out[6], and_1_out[7], and_1_out[8], and_1_out[9], and_1_out[10], and_1_out[11], and_1_out[12], and_1_out[13], and_1_out[14], and_1_out[15], and_1_out[16], and_1_out[17], and_1_out[18], and_1_out[19], and_1_out[20], and_1_out[21], and_1_out[22], and_1_out[23], and_1_out[24], and_1_out[25], and_1_out[26], and_1_out[27], and_1_out[28], and_1_out[29], and_1_out[30], and_1_out[31], and_1_out[32], and_1_out[33], and_1_out[34], and_1_out[35], and_1_out[36], and_1_out[37], and_1_out[38], and_1_out[39], and_1_out[40], and_1_out[41], and_1_out[42], and_1_out[43], and_1_out[44], and_1_out[45], and_1_out[46], and_1_out[47], and_1_out[48]);
endmodule

module win_pos_diagonal (
  input  [48:0] S,
  output W
);

  wire [48:0] and_1_out;

  assign and_1_out = S & {S[42:0], {6{1'b0}}} & {S[36:0], {12{1'b0}}} & {S[30:0], {18{1'b0}}};  // AND_Gate and_1, 49 bits wide
  or or_1 (W, and_1_out[0], and_1_out[1], and_1_out[2], and_1_out[3], and_1_out[4], and_1_out[5], and_1_out[6], and_1_out[7], and_1_out[8], and_1_out[9], and_1_out[10], and_1_out[11], and_1_out[12], and_1_out[13], and_1_out[14], and_1_out[15], and_1_out[16], and_1_out[17], and_1_out[18], and_1_out[19], and_1_out[20], and_1_out[21], and_1_out[22], and_1_out[23], and_1_out[24], and_1_out[25], and_1_out[26], and_1_out[27], and_1_out[28], and_1_out[29], and_1_out[30], and_1_out[31], and_1_out[32], and_1_out[33], and_1_out[34], and_1_out[35], and_1_out[36], and_1_out[37], and_1_out[38], and_1_out[39], and_1_out[40], and_1_out[41], and_1_out[42], and_1_out[43], and_1_out[44], and_1_out[45], and_1_out[46], and_1_out[47], and_1_out[48]);
endmodule

module win_neg_diagonal (
  input  [48:0] S,
  output W
);

  wire [48:0] and_1_out;

  assign and_1_out = S & {S[40:0], {8{1'b0}}} & {S[32:0], {16{1'b0}}} & {S[24:0], {24{1'b0}}};  // AND_Gate and_1, 49 bits wide
  or or_1 (W, and_1_out[0], and_1_out[1], and_1_out[2], and_1_out[3], and_1_out[4], and_1_out[5], and_1_out[6], and_1_out[7], and_1_out[8], and_1_out[9], and_1_out[10], and_1_out[11], and_1_out[12], and_1_out[13], and_1_out[14], and_1_out[15], and_1_out[16], and_1_out[17], and_1_out[18], and_1_out[19], and_1_out[20], and_1_out[21], and_1_out[22], and_1_out[23], and_1_out[24], and_1_out[25], and_1_out[26], and_1_out[27], and_1_out[28], and_1_out[29], and_1_out[30], and_1_out[31], and_1_out[32], and_1_out[33], and_1_out[34], and_1_out[35], and_1_out[36], and_1_out[37], and_1_out[38], and_1_out[39], and_1_out[40], and_1_out[41], and_1_out[42], and_1_out[43], and_1_out[44], and_1_out[45], and_1_out[46], and_1_out[47], and_1_out[48]);
endmodule

module player_display (
  input  [1:0] in_1
);

  wire not_1_out, not_2_out;
  wire [1:0] and_2_out;

  not not_1 (not_1_out, in_1[0]);
  not not_2 (not_2_out, in_1[1]);
  color_decoder color_decoder_1 (.P(and_2_out));  // open: G, R, B
  and and_1 (and_2_out[1], in_1[1], not_1_out);
  and and_2 (and_2_out[0], not_2_out, in_1[0]);
  // RGBLED rgbled_1: pin names not known
endmodule

module draw_check (
  input  [48:0] S,
  output D
);

  wire [5:0] and_1_out;

  assign {D, and_1_out} = S[6:0] & S[13:7] & S[20:14] & S[27:21] & S[34:28] & S[41:35] & S[48:42];  // AND_Gate and_1, 7 bits wide
endmodule

module win_check (
  input  [48:0] S,
  output W
);

  wire win_horizontal_1_w, win_neg_diagonal_1_w, win_pos_diagonal_1_w, win_vertical_1_w;
  wire [48:0] remove_highest_bit_board_1_s_new;

  remove_highest_bit_board remove_highest_bit_board_1 (.S(S), .S_new(remove_highest_bit_board_1_s_new));
  win_vertical win_vertical_1 (.S(remove_highest_bit_board_1_s_new), .W(win_vertical_1_w));
  win_horizontal win_horizontal_1 (.S(remove_highest_bit_board_1_s_new), .W(win_horizontal_1_w));
  win_pos_diagonal win_pos_diagonal_1 (.S(remove_highest_bit_board_1_s_new), .W(win_pos_diagonal_1_w));
  win_neg_diagonal win_neg_diagonal_1 (.S(remove_highest_bit_board_1_s_new), .W(win_neg_diagonal_1_w));
  or or_1 (W, win_vertical_1_w, win_horizontal_1_w, win_pos_diagonal_1_w, win_neg_diagonal_1_w);
endmodule
